// Logisim project project.circ as structural Verilog: 3 circuits, main circuit main
module main (
);

  wire button_1_out, button_2_out, or_1_out;
  wire [31:0] counter_1_q, t_block_1_out_4, t_block_2_out_4, t_block_3_out_4, t_block_4_out_4, undriven_12,
       undriven_17, undriven_18, undriven_19, undriven_20, undriven_21, undriven_22, undriven_23,
       undriven_24, undriven_25, undriven_26, undriven_27, undriven_28;
  wire [31:1] undriven, undriven_2, undriven_3, undriven_4, undriven_5, undriven_6, undriven_7, undriven_8,
       undriven_9, undriven_10, undriven_11, undriven_13, undriven_14, undriven_15, undriven_16;
  wire [31:10] \трансформатор_1_out_2 ;

  T_block t_block_1 (
    .cur(\трансформатор_1_out_2 [19]), .left(\трансформатор_1_out_2 [20]), .out_4(t_block_1_out_4[0]),
    .fight(\трансформатор_1_out_2 [18]));
  T_block t_block_2 (
    .cur(\трансформатор_1_out_2 [20]), .left(\трансформатор_1_out_2 [21]), .out_4(t_block_2_out_4[0]),
    .fight(\трансформатор_1_out_2 [19]));
  T_block t_block_3 (
    .cur(\трансформатор_1_out_2 [18]), .left(\трансформатор_1_out_2 [19]), .out_4(t_block_3_out_4[0]),
    .fight(\трансформатор_1_out_2 [17]));
  T_block t_block_4 (
    .cur(\трансформатор_1_out_2 [17]), .left(\трансформатор_1_out_2 [18]), .out_4(t_block_4_out_4[0]),
    .fight(\трансформатор_1_out_2 [16]));
  DotMatrix #(.matrixcols(32), .matrixrows(32)) dotmatrix_1 (
    .col0({undriven_2, \трансформатор_1_out_2 [31]}), .col1({undriven_3, \трансформатор_1_out_2 [30]}),
    .col2({undriven_4, \трансформатор_1_out_2 [29]}), .col3({undriven_5, \трансформатор_1_out_2 [28]}),
    .col4({undriven_6, \трансформатор_1_out_2 [27]}), .col5({undriven_7, \трансформатор_1_out_2 [26]}),
    .col6({undriven_8, \трансформатор_1_out_2 [25]}), .col7({undriven_9, \трансформатор_1_out_2 [24]}),
    .col8({undriven_10, \трансформатор_1_out_2 [23]}), .col9({undriven, \трансформатор_1_out_2 [22]}),
    .col10({undriven_11, \трансформатор_1_out_2 [21]}),
    .col11({t_block_2_out_4[31:2], \трансформатор_1_out_2 [20], t_block_2_out_4[0]}),
    .col12({t_block_1_out_4[31:2], \трансформатор_1_out_2 [19], t_block_1_out_4[0]}),
    .col13({t_block_3_out_4[31:2], \трансформатор_1_out_2 [18], t_block_3_out_4[0]}),
    .col14({t_block_4_out_4[31:2], \трансформатор_1_out_2 [17], t_block_4_out_4[0]}),
    .col15({undriven_12[31:2], \трансформатор_1_out_2 [16], undriven_12[0]}),
    .col16({undriven_13, \трансформатор_1_out_2 [15]}), .col17(undriven_24),
    .col18({undriven_14, \трансформатор_1_out_2 [13]}), .col19({undriven_15, \трансформатор_1_out_2 [12]}),
    .col20(undriven_25), .col21({undriven_16, \трансформатор_1_out_2 [10]}), .col22(undriven_22),
    .col23(undriven_26), .col24(undriven_17), .col25(undriven_18), .col26(undriven_28), .col27(undriven_19),
    .col28(undriven_27), .col29(undriven_20), .col30(undriven_21), .col31(undriven_23));
  Button button_1 (.out(button_1_out));
  Button button_2 (.out(button_2_out));
  // Probe on counter_1_q
  Counter #(.width(32), .max('h1f)) counter_1 (
    .load(button_1_out), .Q(counter_1_q), .clk(or_1_out));  // open: D, count, carry, clr
  or or_1 (or_1_out, button_1_out, button_2_out);
  \трансформатор  \u_трансформатор_1  (
    .in_1(counter_1_q[4:0]),
    .out_2({\трансформатор_1_out_2 [31:15], undriven_24[0], \трансформатор_1_out_2 [13:12], undriven_25[0], \трансформатор_1_out_2 [10], undriven_22[0], undriven_26[0], undriven_17[0], undriven_18[0], undriven_28[0], undriven_19[0], undriven_27[0], undriven_20[0], undriven_21[0], undriven_23[0]}));
endmodule

module \трансформатор  (
  input  [4:0] in_1,
  output [31:0] out_2
);

  Comparator #(.width(5), .mode("unsigned")) comparator_1 (.a(in_1), .b({5{1'b0}}), .eq(out_2[0]));  // open: gt, lt
  Comparator #(.width(5), .mode("unsigned")) comparator_2 (.a(in_1), .b(5'b00001), .eq(out_2[1]));  // open: gt, lt
  Comparator #(.width(5), .mode("unsigned")) comparator_3 (.a(in_1), .b(5'b00010), .eq(out_2[2]));  // open: gt, lt
  Comparator #(.width(5), .mode("unsigned")) comparator_4 (.a(in_1), .b(5'b00011), .eq(out_2[3]));  // open: gt, lt
  Comparator #(.width(5), .mode("unsigned")) comparator_5 (.a(in_1), .b(5'b00100), .eq(out_2[4]));  // open: gt, lt
  Comparator #(.width(5), .mode("unsigned")) comparator_6 (.a(in_1), .b(5'b00101), .eq(out_2[5]));  // open: gt, lt
  Comparator #(.width(5), .mode("unsigned")) comparator_7 (.a(in_1), .b(5'b00110), .eq(out_2[6]));  // open: gt, lt
  Comparator #(.width(5), .mode("unsigned")) comparator_8 (.a(in_1), .b(5'b00111), .eq(out_2[7]));  // open: gt, lt
  Comparator #(.width(5), .mode("unsigned")) comparator_9 (.a(in_1), .b(5'b01000), .eq(out_2[8]));  // open: gt, lt
  Comparator #(.width(5), .mode("unsigned")) comparator_10 (.a(in_1), .b(5'b01001), .eq(out_2[9]));  // open: gt, lt
  Comparator #(.width(5), .mode("unsigned")) comparator_11 (.a(in_1), .b(5'b01010), .eq(out_2[10]));  // open: gt, lt
  Comparator #(.width(5), .mode("unsigned")) comparator_12 (.a(in_1), .b(5'b01011), .eq(out_2[11]));  // open: gt, lt
  Comparator #(.width(5), .mode("unsigned")) comparator_13 (.a(in_1), .b(5'b01100), .eq(out_2[12]));  // open: gt, lt
  Comparator #(.width(5), .mode("unsigned")) comparator_14 (.a(in_1), .b(5'b01101), .eq(out_2[13]));  // open: gt, lt
  Comparator #(.width(5), .mode("unsigned")) comparator_15 (.a(in_1), .b(5'b01110), .eq(out_2[14]));  // open: gt, lt
  Comparator #(.width(5), .mode("unsigned")) comparator_16 (.a(in_1), .b(5'b01111), .eq(out_2[15]));  // open: gt, lt
  Comparator #(.width(5), .mode("unsigned")) comparator_17 (.a(in_1), .b(5'b10000), .eq(out_2[16]));  // open: gt, lt
  Comparator #(.width(5), .mode("unsigned")) comparator_18 (.a(in_1), .b(5'b10001), .eq(out_2[17]));  // open: gt, lt
  Comparator #(.width(5), .mode("unsigned")) comparator_19 (.a(in_1), .b(5'b10010), .eq(out_2[18]));  // open: gt, lt
  Comparator #(.width(5), .mode("unsigned")) comparator_20 (.a(in_1), .b(5'b10011), .eq(out_2[19]));  // open: gt, lt
  Comparator #(.width(5), .mode("unsigned")) comparator_21 (.a(in_1), .b(5'b10100), .eq(out_2[20]));  // open: gt, lt
  Comparator #(.width(5), .mode("unsigned")) comparator_22 (.a(in_1), .b(5'b10101), .eq(out_2[21]));  // open: gt, lt
  Comparator #(.width(5), .mode("unsigned")) comparator_23 (.a(in_1), .b(5'b10110), .eq(out_2[22]));  // open: gt, lt
  Comparator #(.width(5), .mode("unsigned")) comparator_24 (.a(in_1), .b(5'b10111), .eq(out_2[23]));  // open: gt, lt
  Comparator #(.width(5), .mode("unsigned")) comparator_25 (.a(in_1), .b(5'b11000), .eq(out_2[24]));  // open: gt, lt
  Comparator #(.width(5), .mode("unsigned")) comparator_26 (.a(in_1), .b(5'b11001), .eq(out_2[25]));  // open: gt, lt
  Comparator #(.width(5), .mode("unsigned")) comparator_27 (.a(in_1), .b(5'b11010), .eq(out_2[26]));  // open: gt, lt
  Comparator #(.width(5), .mode("unsigned")) comparator_28 (.a(in_1), .b(5'b11011), .eq(out_2[27]));  // open: gt, lt
  Comparator #(.width(5), .mode("unsigned")) comparator_29 (.a(in_1), .b(5'b11100), .eq(out_2[28]));  // open: gt, lt
  Comparator #(.width(5), .mode("unsigned")) comparator_30 (.a(in_1), .b(5'b11101), .eq(out_2[29]));  // open: gt, lt
  Comparator #(.width(5), .mode("unsigned")) comparator_31 (.a(in_1), .b(5'b11110), .eq(out_2[30]));  // open: gt, lt
  Comparator #(.width(5), .mode("unsigned")) comparator_32 (.a(in_1), .b({5{1'b1}}), .eq(out_2[31]));  // open: gt, lt
endmodule

module T_block (
  input  cur,
  input  left,
  input  fight,
  output out_4
);

  or or_1 (out_4, cur, left, fight);
endmodule
